// Logisim project mips-datapath-lab-aoc1.circ as structural Verilog: 7 circuits, main circuit mips
module alu (
  input  [3:0] ALU_Control,
  input  [31:0] in_2,
  input  [31:0] in_3,
  output [31:0] out_4,
  output Zero
);

  wire comparator_1_lt;
  wire [31:0] adder_1_out, and_1_out, multiplexer_1_out, or_1_out, subtractor_1_out, xor_1_out;

  assign and_1_out = in_2 & in_3;  // AND_Gate and_1, 32 bits wide
  assign or_1_out = in_2 | in_3;  // OR_Gate or_1, 32 bits wide
  Adder #(.width(32)) adder_1 (.a(in_2), .b(in_3), .out(adder_1_out));  // open: cin, cout
  Subtractor #(.width(32)) subtractor_1 (.a(in_2), .b(in_3), .out(subtractor_1_out));  // open: bin, bout
  Comparator #(.width(32), .mode("unsigned")) comparator_1 (.a(in_2), .b(in_3), .lt(comparator_1_lt));  // open: gt, eq
  assign xor_1_out = in_2 ^ in_3;  // XOR_Gate xor_1, 32 bits wide
  Multiplexer #(.width(32), .enable("false")) multiplexer_1 (
    .in0({32{1'b0}}), .in1(32'h1), .out(multiplexer_1_out), .sel(comparator_1_lt));
  Multiplexer #(.select(4), .width(32), .disabled(0), .enable("false")) multiplexer_2 (
    .in0(and_1_out), .in1(or_1_out), .in2(adder_1_out), .in6(subtractor_1_out), .in7(multiplexer_1_out),
    .in12(xor_1_out), .out(out_4), .sel(ALU_Control));  // open: in3, in4, in5, in8, in9, in10, in11, in13, in14, in15
  Comparator #(.width(32), .mode("unsigned")) comparator_2 (.a(out_4), .b({32{1'b0}}), .eq(Zero));  // open: gt, lt

  // Notes on the sheet:
  //   A
  //   B
  //   Op selects the result
  //   Output
endmodule

module mips (
);

  wire alu_1_zero, ALUSrc, and_1_out, Branch, clock_1_out, control_1_regwrite, Jump, MemRead, MemtoReg,
       MemWrite, RegDst, Restart_Program_out, Zero_Reg_File_out;
  wire [1:0] ALUOp;
  wire [3:0] alu_control_1_operation;
  wire [4:0] multiplexer_1_out;
  wire [7:0] alu_1_out_4_2;
  wire [27:0] bit_extender_1_out, shifter_1_out;
  wire [31:0] adder_1_out, adder_2_out, alu_1_out_4, bit_extender_2_out, multiplexer_2_out,
       multiplexer_3_out, multiplexer_4_out, multiplexer_5_out, PC_q, ram_1_data, reg_32_1_readdata1,
       reg_32_1_readdata2, rom_1_data, shifter_2_out;

  Register #(.width(32)) PC (
    .D(multiplexer_4_out), .Q(PC_q), .clk(clock_1_out), .clr(Restart_Program_out));  // open: en
  Clock clock_1 (.out(clock_1_out));
  Button Restart_Program (.out(Restart_Program_out));
  Button Zero_Reg_File (.out(Zero_Reg_File_out));
  Adder #(.width(32)) adder_1 (.a(PC_q), .b(32'h4), .out(adder_1_out));  // open: cin, cout
  // Probe on rom_1_data
  // Probe on rom_1_data[31:26]
  assign bit_extender_1_out = {{2{rom_1_data[25]}}, rom_1_data[25:0]};  // Bit_Extender bit_extender_1
  ROM #(.dataWidth(32)) rom_1 (.addr(PC_q[9:2]), .data(rom_1_data));  // open: sel
  Shifter #(.width(28)) shifter_1 (.in(bit_extender_1_out), .\dist (5'b00010), .out(shifter_1_out));
  Multiplexer #(.width(5), .enable("false")) multiplexer_1 (
    .in0(rom_1_data[20:16]), .in1(rom_1_data[15:11]), .out(multiplexer_1_out), .sel(RegDst));
  control control_1 (
    .in_1(rom_1_data[31:26]), .RegDst(RegDst), .Branch(Branch), .MemRead(MemRead), .MemtoReg(MemtoReg),
    .ALUOp(ALUOp), .MemWrite(MemWrite), .ALUSrc(ALUSrc), .RegWrite(control_1_regwrite), .Jump(Jump));
  // Probe on multiplexer_5_out
  reg_32 reg_32_1 (
    .ReadReg1(rom_1_data[25:21]), .ReadReg2(rom_1_data[20:16]), .WriteReg(multiplexer_1_out),
    .RegWrite(control_1_regwrite), .ReadData1(reg_32_1_readdata1), .ReadData2(reg_32_1_readdata2),
    .WriteData(multiplexer_5_out), .Clk(clock_1_out), .Reset(Zero_Reg_File_out));
  // Probe on rom_1_data[25:21]
  // Probe on rom_1_data[20:16]
  // Probe on multiplexer_1_out
  assign bit_extender_2_out = {{16{rom_1_data[15]}}, rom_1_data[15:0]};  // Bit_Extender bit_extender_2
  Multiplexer #(.width(32), .enable("false")) multiplexer_2 (
    .in0(reg_32_1_readdata2), .in1(bit_extender_2_out), .out(multiplexer_2_out), .sel(ALUSrc));
  // Probe on bit_extender_2_out
  alu_control alu_control_1 (.Operation(alu_control_1_operation), .ALUOp(ALUOp), .Function(rom_1_data[5:0]));
  Shifter #(.width(32)) shifter_2 (.in(bit_extender_2_out), .\dist (5'b00010), .out(shifter_2_out));
  alu alu_1 (
    .out_4({alu_1_out_4[31:10], alu_1_out_4_2, alu_1_out_4[1:0]}), .Zero(alu_1_zero),
    .in_2(reg_32_1_readdata1), .in_3(multiplexer_2_out), .ALU_Control(alu_control_1_operation));
  // Probe on reg_32_1_readdata1
  // Probe on multiplexer_2_out
  Adder #(.width(32)) adder_2 (.a(adder_1_out), .b(shifter_2_out), .out(adder_2_out));  // open: cin, cout
  and and_1 (and_1_out, Branch, alu_1_zero);
  // Probe on alu_control_1_operation
  Multiplexer #(.width(32), .enable("false")) multiplexer_3 (
    .in0(adder_1_out), .in1(adder_2_out), .out(multiplexer_3_out), .sel(and_1_out));
  // Probe on multiplexer_4_out
  Multiplexer #(.width(32), .enable("false")) multiplexer_4 (
    .in0(multiplexer_3_out), .in1({adder_1_out[31:28], shifter_1_out}), .out(multiplexer_4_out), .sel(Jump));
  // Probe on alu_1_out_4_2
  RAM #(.dataWidth(32), .bus("separate")) ram_1 (
    .addr(alu_1_out_4_2), .din(reg_32_1_readdata2), .data(ram_1_data), .str(MemWrite), .clk(clock_1_out),
    .ld(MemRead));  // open: sel, clr
  Multiplexer #(.width(32), .enable("false")) multiplexer_5 (
    .in0({alu_1_out_4[31:10], alu_1_out_4_2, alu_1_out_4[1:0]}), .in1(ram_1_data), .out(multiplexer_5_out),
    .sel(MemtoReg));
  // Probe on multiplexer_5_out

  // Notes on the sheet:
  //   Clock
  //   Current Instruction
  //   contents of rom_1 (hex, n*v repeats v):
  //   8c080000 4820 11000003 1284820 2108ffff 8100002 ac090004
  //   PC+4 [31-28]
  //   jump address
  //   Reg Write Data
  //   Imm. Value
  //   ALU Op
  //   Next PC
  //   Mem Addr
  //   Right-click and load the 1234.mem into the RAM.
endmodule

module instruction_type_decode (
  input  [5:0] opcode,
  output R_format,
  output lw,
  output sw,
  output beq,
  output addi,
  output j
);

  Comparator #(.width(6), .mode("unsigned")) comparator_1 (.a({6{1'b0}}), .b(opcode), .eq(R_format));  // open: gt, lt
  Comparator #(.width(6), .mode("unsigned")) comparator_2 (.a(6'b100011), .b(opcode), .eq(lw));  // open: gt, lt
  Comparator #(.width(6), .mode("unsigned")) comparator_3 (.a(6'b101011), .b(opcode), .eq(sw));  // open: gt, lt
  Comparator #(.width(6), .mode("unsigned")) comparator_4 (.a(6'b000100), .b(opcode), .eq(beq));  // open: gt, lt
  Comparator #(.width(6), .mode("unsigned")) comparator_5 (.a(6'b001000), .b(opcode), .eq(addi));  // open: gt, lt
  Comparator #(.width(6), .mode("unsigned")) comparator_6 (.a(6'b000010), .b(opcode), .eq(j));  // open: gt, lt
endmodule

module control_decode (
  input  Rformat,
  input  lw,
  input  sw,
  input  beq,
  input  addi,
  input  j,
  output RegDst,
  output ALUSrc,
  output MemtoReg,
  output RegWrite,
  output MemRead,
  output MemWrite,
  output Branch,
  output ALUOp1,
  output ALUOp0,
  output Jump
);

  wire and_2_out, not_1_out, not_2_out, not_3_out, not_4_out, not_5_out, not_6_out;

  not not_1 (not_1_out, Rformat);
  not not_2 (not_2_out, beq);
  not not_3 (not_3_out, j);
  not not_4 (not_4_out, sw);
  not not_5 (not_5_out, beq);
  not not_6 (not_6_out, j);
  and and_1 (ALUSrc, not_1_out, not_2_out, not_3_out);
  and and_2 (and_2_out, not_4_out, not_5_out, addi, not_6_out);
  or or_1 (RegWrite, and_2_out, lw, Rformat);

  assign ALUOp0 = beq;
  assign ALUOp1 = Rformat;
  assign Branch = beq;
  assign Jump = j;
  assign MemRead = lw;
  assign MemtoReg = lw;
  assign MemWrite = sw;
  assign RegDst = Rformat;
endmodule

module alu_control (
  input  [5:0] Function,
  input  [1:0] ALUOp,
  output [3:0] Operation
);

  wire A_out, B_out, C_out, D_out, E_out, F_out, G_out, H_out, I_out;
  wire [2:0] priority_encoder_1_out;

  and A (A_out, ~ALUOp[1], ~ALUOp[0]);  // AND_Gate
  and C (C_out, ALUOp[1], ~ALUOp[0], ~Function[3], ~Function[2], ~Function[1], ~Function[0]);  // AND_Gate
  and D (D_out, ~ALUOp[1], ALUOp[0]);  // AND_Gate
  and F (F_out, ALUOp[1], ~Function[3], ~Function[2], Function[1], ~Function[0]);  // AND_Gate
  and G (G_out, ALUOp[1], ~ALUOp[0], ~Function[3], Function[2], ~Function[1], ~Function[0]);  // AND_Gate
  and H (H_out, ALUOp[1], ~ALUOp[0], ~Function[3], Function[2], ~Function[1], Function[0]);  // AND_Gate
  and I (I_out, ALUOp[1], Function[3], ~Function[2], Function[1], ~Function[0]);  // AND_Gate
  or B (B_out, A_out, C_out);
  or E (E_out, D_out, F_out);
  Priority_Encoder priority_encoder_1 (
    .in0(G_out), .in1(H_out), .in2(B_out), .in3(E_out), .in4(I_out), .out(priority_encoder_1_out));  // open: in5, in6, in7, en_in, gs, en_out
  Multiplexer #(.select(3), .width(4)) multiplexer_1 (
    .in0(4'b0000), .in1(4'b0001), .in2(4'b0010), .in3(4'b0110), .in4(4'b0111), .out(Operation),
    .sel(priority_encoder_1_out));  // open: in5, in6, in7, en

  // Notes on the sheet:
  //   Inputs
  //   B -- OR
  //   Hint: Here is the logic for the first row: 
  //   A -- if (ALUOp1=0 and ALUOp0=0)
  //   OUTPUT -- then output = 2 = 0010
  //   E -- OR
  //   C -- if (ALUOp1=1 and ALUOp0=0 and F3, F2, F1, F0 are all 0)
  //   D -- if (ALUOP1=0 and ALUOP0=1
  //   F -- if (ALUOP1=1 and F3,F2,F0=0 and F1=1)
  //   G -- if (ALUOP1=1 and ALUOP0=0 and F3,F1,F0=0 and F2=1)
  //   H -- if (ALUOP1=1 and ALUOP0=0 and F3,F1=0 and F2,F0=1)
  //   I -- if (ALUOP1=1 and F3,F1=1 and F2,F0=0)
  //   True for 0010=2
  //   True for 0110=6
  //   True for 0001=1
  //   True for 0111=7
  //   True for 0000=0
  //   We have 5 possible outputs
  //   D
  //   Depending on which input is 1,
  //   one of the outputs above will be selected.
endmodule

module control (
  input  [5:0] in_1,
  output RegDst,
  output Jump,
  output Branch,
  output MemRead,
  output MemtoReg,
  output [1:0] ALUOp,
  output MemWrite,
  output ALUSrc,
  output RegWrite
);

  wire instruction_type_decode_1_addi, instruction_type_decode_1_beq, instruction_type_decode_1_j,
       instruction_type_decode_1_lw, instruction_type_decode_1_r_format, instruction_type_decode_1_sw;

  instruction_type_decode instruction_type_decode_1 (
    .opcode(in_1), .R_format(instruction_type_decode_1_r_format), .lw(instruction_type_decode_1_lw),
    .sw(instruction_type_decode_1_sw), .beq(instruction_type_decode_1_beq),
    .addi(instruction_type_decode_1_addi), .j(instruction_type_decode_1_j));
  control_decode control_decode_1 (
    .Rformat(instruction_type_decode_1_r_format), .RegDst(RegDst), .lw(instruction_type_decode_1_lw),
    .ALUSrc(ALUSrc), .sw(instruction_type_decode_1_sw), .MemtoReg(MemtoReg),
    .beq(instruction_type_decode_1_beq), .addi(instruction_type_decode_1_addi),
    .j(instruction_type_decode_1_j), .RegWrite(RegWrite), .MemRead(MemRead), .MemWrite(MemWrite),
    .Branch(Branch), .ALUOp1(ALUOp[1]), .ALUOp0(ALUOp[0]), .Jump(Jump));

  // Notes on the sheet:
  //   Instruction OpCode
  //   Decode the Instruction Type first
  //   From the Insturction Type,
  //   decode the control signals
endmodule

module reg_32 (
  input  [4:0] ReadReg1,
  input  [4:0] ReadReg2,
  input  [4:0] WriteReg,
  input  RegWrite,
  input  [31:0] WriteData,
  input  Clk,
  input  Reset,
  output [31:0] ReadData1,
  output [31:0] ReadData2
);

  wire decoder_1_out0, decoder_1_out1, decoder_2_out0, decoder_2_out1, decoder_2_out2, decoder_2_out3,
       decoder_3_out0, decoder_3_out1, decoder_3_out2, decoder_3_out3, decoder_4_out0, decoder_4_out1,
       decoder_4_out2, decoder_4_out3, decoder_5_out0, decoder_5_out1, decoder_5_out2, decoder_5_out3,
       decoder_6_out0, decoder_6_out1, decoder_6_out2, decoder_6_out3, decoder_7_out0, decoder_7_out1,
       decoder_7_out2, decoder_7_out3, decoder_8_out0, decoder_8_out1, decoder_8_out2, decoder_8_out3,
       decoder_9_out0, decoder_9_out1, decoder_9_out2, decoder_9_out3, decoder_10_out0, decoder_10_out1,
       decoder_10_out2, decoder_10_out3, decoder_11_out0, decoder_11_out1, decoder_11_out2, decoder_11_out3;
  wire [31:0] multiplexer_1_out, multiplexer_2_out, multiplexer_3_out, multiplexer_4_out, multiplexer_5_out,
       multiplexer_6_out, multiplexer_7_out, multiplexer_8_out, multiplexer_9_out, multiplexer_10_out,
       multiplexer_13_out, multiplexer_14_out, multiplexer_15_out, multiplexer_16_out, multiplexer_17_out,
       multiplexer_18_out, multiplexer_19_out, multiplexer_20_out, multiplexer_21_out, multiplexer_22_out,
       register_1_q, register_2_q, register_3_q, register_4_q, register_5_q, register_6_q, register_7_q,
       register_8_q, register_9_q, register_10_q, register_11_q, register_12_q, register_13_q, register_14_q,
       register_15_q, register_16_q, register_17_q, register_18_q, register_19_q, register_20_q,
       register_21_q, register_22_q, register_23_q, register_24_q, register_25_q, register_26_q,
       register_27_q, register_28_q, register_29_q, register_30_q, register_31_q;

  // Probe on WriteReg
  Decoder #(.disabled(0)) decoder_1 (.out0(decoder_1_out0), .out1(decoder_1_out1), .sel(WriteReg[4]), .en(RegWrite));
  Decoder #(.select(2), .disabled(0)) decoder_2 (
    .out0(decoder_2_out0), .out1(decoder_2_out1), .out2(decoder_2_out2), .out3(decoder_2_out3),
    .sel(WriteReg[3:2]), .en(decoder_1_out0));
  Decoder #(.select(2), .disabled(0)) decoder_3 (
    .out0(decoder_3_out0), .out1(decoder_3_out1), .out2(decoder_3_out2), .out3(decoder_3_out3),
    .sel(WriteReg[1:0]), .en(decoder_2_out0));
  Decoder #(.select(2), .disabled(0)) decoder_4 (
    .out0(decoder_4_out0), .out1(decoder_4_out1), .out2(decoder_4_out2), .out3(decoder_4_out3),
    .sel(WriteReg[1:0]), .en(decoder_2_out1));
  Decoder #(.select(2), .disabled(0)) decoder_5 (
    .out0(decoder_5_out0), .out1(decoder_5_out1), .out2(decoder_5_out2), .out3(decoder_5_out3),
    .sel(WriteReg[1:0]), .en(decoder_2_out2));
  Decoder #(.select(2), .disabled(0)) decoder_6 (
    .out0(decoder_6_out0), .out1(decoder_6_out1), .out2(decoder_6_out2), .out3(decoder_6_out3),
    .sel(WriteReg[1:0]), .en(decoder_2_out3));
  Register #(.width(32)) register_1 (.D(WriteData), .en(decoder_3_out1), .Q(register_1_q), .clk(Clk), .clr(Reset));
  Register #(.width(32)) register_2 (.D(WriteData), .en(decoder_3_out2), .Q(register_2_q), .clk(Clk), .clr(Reset));
  Register #(.width(32)) register_3 (.D(WriteData), .en(decoder_3_out3), .Q(register_3_q), .clk(Clk), .clr(Reset));
  Register #(.width(32)) register_4 (.D(WriteData), .en(decoder_4_out0), .Q(register_4_q), .clk(Clk), .clr(Reset));
  Register #(.width(32)) register_5 (.D(WriteData), .en(decoder_4_out1), .Q(register_5_q), .clk(Clk), .clr(Reset));
  Register #(.width(32)) register_6 (.D(WriteData), .en(decoder_4_out2), .Q(register_6_q), .clk(Clk), .clr(Reset));
  Register #(.width(32)) register_7 (.D(WriteData), .en(decoder_4_out3), .Q(register_7_q), .clk(Clk), .clr(Reset));
  Register #(.width(32)) register_8 (.D(WriteData), .en(decoder_5_out0), .Q(register_8_q), .clk(Clk), .clr(Reset));
  Register #(.width(32)) register_9 (.D(WriteData), .en(decoder_5_out1), .Q(register_9_q), .clk(Clk), .clr(Reset));
  Register #(.width(32)) register_10 (.D(WriteData), .en(decoder_5_out2), .Q(register_10_q), .clk(Clk), .clr(Reset));
  Register #(.width(32)) register_11 (.D(WriteData), .en(decoder_5_out3), .Q(register_11_q), .clk(Clk), .clr(Reset));
  Register #(.width(32)) register_12 (.D(WriteData), .en(decoder_6_out0), .Q(register_12_q), .clk(Clk), .clr(Reset));
  Register #(.width(32)) register_13 (.D(WriteData), .en(decoder_6_out1), .Q(register_13_q), .clk(Clk), .clr(Reset));
  Register #(.width(32)) register_14 (.D(WriteData), .en(decoder_6_out2), .Q(register_14_q), .clk(Clk), .clr(Reset));
  Register #(.width(32)) register_15 (.D(WriteData), .en(decoder_6_out3), .Q(register_15_q), .clk(Clk), .clr(Reset));
  // Probe on {32{1'b0}}
  // Probe on register_1_q
  // Probe on register_2_q
  // Probe on register_3_q
  // Probe on register_4_q
  // Probe on register_5_q
  // Probe on register_6_q
  // Probe on register_7_q
  // Probe on register_8_q
  // Probe on register_9_q
  // Probe on register_10_q
  // Probe on register_11_q
  // Probe on register_12_q
  // Probe on register_13_q
  // Probe on register_14_q
  // Probe on register_15_q
  // Probe on ReadReg1
  Multiplexer #(.select(2), .width(32), .enable("false")) multiplexer_1 (
    .in0({32{1'b0}}), .in1(register_1_q), .in2(register_2_q), .in3(register_3_q), .out(multiplexer_1_out),
    .sel(ReadReg1[1:0]));
  Multiplexer #(.select(2), .width(32), .enable("false")) multiplexer_2 (
    .in0(register_4_q), .in1(register_5_q), .in2(register_6_q), .in3(register_7_q), .out(multiplexer_2_out),
    .sel(ReadReg1[1:0]));
  Multiplexer #(.select(2), .width(32), .enable("false")) multiplexer_3 (
    .in0(register_8_q), .in1(register_9_q), .in2(register_10_q), .in3(register_11_q),
    .out(multiplexer_3_out), .sel(ReadReg1[1:0]));
  Multiplexer #(.select(2), .width(32), .enable("false")) multiplexer_4 (
    .in0(register_12_q), .in1(register_13_q), .in2(register_14_q), .in3(register_15_q),
    .out(multiplexer_4_out), .sel(ReadReg1[1:0]));
  // Probe on ReadReg2
  Multiplexer #(.select(2), .width(32), .enable("false")) multiplexer_5 (
    .in0({32{1'b0}}), .in1(register_1_q), .in2(register_2_q), .in3(register_3_q), .out(multiplexer_5_out),
    .sel(ReadReg2[1:0]));
  Multiplexer #(.select(2), .width(32), .enable("false")) multiplexer_6 (
    .in0(register_4_q), .in1(register_5_q), .in2(register_6_q), .in3(register_7_q), .out(multiplexer_6_out),
    .sel(ReadReg2[1:0]));
  Multiplexer #(.select(2), .width(32), .enable("false")) multiplexer_7 (
    .in0(register_8_q), .in1(register_9_q), .in2(register_10_q), .in3(register_11_q),
    .out(multiplexer_7_out), .sel(ReadReg2[1:0]));
  Multiplexer #(.select(2), .width(32), .enable("false")) multiplexer_8 (
    .in0(register_12_q), .in1(register_13_q), .in2(register_14_q), .in3(register_15_q),
    .out(multiplexer_8_out), .sel(ReadReg2[1:0]));
  Multiplexer #(.select(2), .width(32), .enable("false")) multiplexer_9 (
    .in0(multiplexer_5_out), .in1(multiplexer_6_out), .in2(multiplexer_7_out), .in3(multiplexer_8_out),
    .out(multiplexer_9_out), .sel(ReadReg2[3:2]));
  Multiplexer #(.select(2), .width(32), .enable("false")) multiplexer_10 (
    .in0(multiplexer_1_out), .in1(multiplexer_2_out), .in2(multiplexer_3_out), .in3(multiplexer_4_out),
    .out(multiplexer_10_out), .sel(ReadReg1[3:2]));
  Decoder #(.select(2), .disabled(0)) decoder_7 (
    .out0(decoder_7_out0), .out1(decoder_7_out1), .out2(decoder_7_out2), .out3(decoder_7_out3),
    .sel(WriteReg[3:2]), .en(decoder_1_out1));
  Decoder #(.select(2), .disabled(0)) decoder_8 (
    .out0(decoder_8_out0), .out1(decoder_8_out1), .out2(decoder_8_out2), .out3(decoder_8_out3),
    .sel(WriteReg[1:0]), .en(decoder_7_out0));
  Decoder #(.select(2), .disabled(0)) decoder_9 (
    .out0(decoder_9_out0), .out1(decoder_9_out1), .out2(decoder_9_out2), .out3(decoder_9_out3),
    .sel(WriteReg[1:0]), .en(decoder_7_out1));
  Decoder #(.select(2), .disabled(0)) decoder_10 (
    .out0(decoder_10_out0), .out1(decoder_10_out1), .out2(decoder_10_out2), .out3(decoder_10_out3),
    .sel(WriteReg[1:0]), .en(decoder_7_out2));
  Decoder #(.select(2), .disabled(0)) decoder_11 (
    .out0(decoder_11_out0), .out1(decoder_11_out1), .out2(decoder_11_out2), .out3(decoder_11_out3),
    .sel(WriteReg[1:0]), .en(decoder_7_out3));
  Register #(.width(32)) register_16 (.D(WriteData), .en(decoder_8_out0), .Q(register_16_q), .clk(Clk), .clr(Reset));
  Register #(.width(32)) register_17 (.D(WriteData), .en(decoder_8_out1), .Q(register_17_q), .clk(Clk), .clr(Reset));
  Register #(.width(32)) register_18 (.D(WriteData), .en(decoder_8_out2), .Q(register_18_q), .clk(Clk), .clr(Reset));
  Register #(.width(32)) register_19 (.D(WriteData), .en(decoder_8_out3), .Q(register_19_q), .clk(Clk), .clr(Reset));
  Register #(.width(32)) register_20 (.D(WriteData), .en(decoder_9_out0), .Q(register_20_q), .clk(Clk), .clr(Reset));
  Register #(.width(32)) register_21 (.D(WriteData), .en(decoder_9_out1), .Q(register_21_q), .clk(Clk), .clr(Reset));
  Register #(.width(32)) register_22 (.D(WriteData), .en(decoder_9_out2), .Q(register_22_q), .clk(Clk), .clr(Reset));
  Register #(.width(32)) register_23 (.D(WriteData), .en(decoder_9_out3), .Q(register_23_q), .clk(Clk), .clr(Reset));
  Register #(.width(32)) register_24 (.D(WriteData), .en(decoder_10_out0), .Q(register_24_q), .clk(Clk), .clr(Reset));
  Register #(.width(32)) register_25 (.D(WriteData), .en(decoder_10_out1), .Q(register_25_q), .clk(Clk), .clr(Reset));
  Register #(.width(32)) register_26 (.D(WriteData), .en(decoder_10_out2), .Q(register_26_q), .clk(Clk), .clr(Reset));
  Register #(.width(32)) register_27 (.D(WriteData), .en(decoder_10_out3), .Q(register_27_q), .clk(Clk), .clr(Reset));
  Register #(.width(32)) register_28 (.D(WriteData), .en(decoder_11_out0), .Q(register_28_q), .clk(Clk), .clr(Reset));
  Register #(.width(32)) register_29 (.D(WriteData), .en(decoder_11_out1), .Q(register_29_q), .clk(Clk), .clr(Reset));
  Register #(.width(32)) register_30 (.D(WriteData), .en(decoder_11_out2), .Q(register_30_q), .clk(Clk), .clr(Reset));
  Register #(.width(32)) register_31 (.D(WriteData), .en(decoder_11_out3), .Q(register_31_q), .clk(Clk), .clr(Reset));
  // Probe on register_16_q
  // Probe on register_17_q
  // Probe on register_18_q
  // Probe on register_19_q
  // Probe on register_20_q
  // Probe on register_21_q
  // Probe on register_22_q
  // Probe on register_23_q
  // Probe on register_24_q
  // Probe on register_25_q
  // Probe on register_26_q
  // Probe on register_27_q
  // Probe on register_28_q
  // Probe on register_29_q
  // Probe on register_30_q
  // Probe on register_31_q
  Multiplexer #(.width(32), .enable("false")) multiplexer_11 (
    .in0(multiplexer_10_out), .in1(multiplexer_21_out), .out(ReadData1), .sel(ReadReg1[4]));
  Multiplexer #(.width(32), .enable("false")) multiplexer_12 (
    .in0(multiplexer_9_out), .in1(multiplexer_22_out), .out(ReadData2), .sel(ReadReg2[4]));
  Multiplexer #(.select(2), .width(32), .enable("false")) multiplexer_13 (
    .in0(register_16_q), .in1(register_17_q), .in2(register_18_q), .in3(register_19_q),
    .out(multiplexer_13_out), .sel(ReadReg1[1:0]));
  Multiplexer #(.select(2), .width(32), .enable("false")) multiplexer_14 (
    .in0(register_20_q), .in1(register_21_q), .in2(register_22_q), .in3(register_23_q),
    .out(multiplexer_14_out), .sel(ReadReg1[1:0]));
  Multiplexer #(.select(2), .width(32), .enable("false")) multiplexer_15 (
    .in0(register_24_q), .in1(register_25_q), .in2(register_26_q), .in3(register_27_q),
    .out(multiplexer_15_out), .sel(ReadReg1[1:0]));
  Multiplexer #(.select(2), .width(32), .enable("false")) multiplexer_16 (
    .in0(register_28_q), .in1(register_29_q), .in2(register_30_q), .in3(register_31_q),
    .out(multiplexer_16_out), .sel(ReadReg1[1:0]));
  Multiplexer #(.select(2), .width(32), .enable("false")) multiplexer_17 (
    .in0(register_16_q), .in1(register_17_q), .in2(register_18_q), .in3(register_19_q),
    .out(multiplexer_17_out), .sel(ReadReg2[1:0]));
  Multiplexer #(.select(2), .width(32), .enable("false")) multiplexer_18 (
    .in0(register_20_q), .in1(register_21_q), .in2(register_22_q), .in3(register_23_q),
    .out(multiplexer_18_out), .sel(ReadReg2[1:0]));
  Multiplexer #(.select(2), .width(32), .enable("false")) multiplexer_19 (
    .in0(register_24_q), .in1(register_25_q), .in2(register_26_q), .in3(register_27_q),
    .out(multiplexer_19_out), .sel(ReadReg2[1:0]));
  Multiplexer #(.select(2), .width(32), .enable("false")) multiplexer_20 (
    .in0(register_28_q), .in1(register_29_q), .in2(register_30_q), .in3(register_31_q),
    .out(multiplexer_20_out), .sel(ReadReg2[1:0]));
  Multiplexer #(.select(2), .width(32), .enable("false")) multiplexer_21 (
    .in0(multiplexer_17_out), .in1(multiplexer_18_out), .in2(multiplexer_19_out), .in3(multiplexer_20_out),
    .out(multiplexer_21_out), .sel(ReadReg2[3:2]));
  Multiplexer #(.select(2), .width(32), .enable("false")) multiplexer_22 (
    .in0(multiplexer_13_out), .in1(multiplexer_14_out), .in2(multiplexer_15_out), .in3(multiplexer_16_out),
    .out(multiplexer_22_out), .sel(ReadReg1[3:2]));
endmodule
